# Fritzing sketch diagrama (saved by Fritzing 1.0.4)
breadboards: 1

parts:
  Componente1 = InvenSense MPU6050
  Mod1 = Heltec WiFi LoRa 32 V2 [part_number=HTIT-WB32LA]
  J1 = Piezo Speaker
  R1 = Resistor [tolerance=±5% resistance=220 package="2010 [SMD]"]
  U1 = LIPO-110mAh [package=lipo-110]

nets:
  N1: Componente1.VCC, Mod1.pin_16, Mod1.pin_17
  GND: Componente1.GND, Mod1.GND, J1.pin1, U1.-
  N2: Componente1.SCL, Mod1.pin_27
  N3: Componente1.SDA, Mod1.pin_1
  N4: Mod1.pin_20, U1.+
  N5: Mod1.pin_21, Mod1.pin_22
  N6: Mod1.pin_29, R1.Pin_1
